# Fritzing sketch Circuit (saved by Fritzing 0.9.0b)
breadboards: 1

parts:
  U1 = atmega328 [package=dip]
  J1 = Piezo Speaker
  LCD1 = LCD screen
  Composant1 = Real Time Clock Module - DS1307 RTC Breakout Board
  Power_plug1 = Power plug
  R1 = Trimmer Potentiometer [maximum_resistance=10kΩ package=THT]

nets:
  N1: U1.D3_(PWM), LCD1.DB6, LCD1.DB7
  N2: U1.D4, LCD1.DB5
  VCC: U1.VCC, U1.AVCC, U1.AREF, LCD1.VDD, Composant1.5V, Power_plug1.VCC, R1.leg2
  GND: U1.GND, J1.pin1, LCD1.VSS, LCD1.R/W, Composant1.GND, Power_plug1.GND, R1.leg1
  N3: U1.D5_(PWM), LCD1.DB4
  N4: U1.D8, J1.pin2
  N5: U1.D12, LCD1.RS
  N6: U1.D13, LCD1.E
  N7: U1.A4, Composant1.SDA
  N8: U1.A5, Composant1.SCL
  N9: LCD1.V0, R1.wiper

notes:
  Haut Bas Gauche Droite Reset Lumiere
